# Fritzing sketch HW (saved by Fritzing 0.9.3b)

parts:
  부품2 = Bluetooth HC-05 Macho
  X1 = USB Connectors [package=usb-a-s-nosilk]
  U1 = LIPO-1000mAh [package=lipo-1000]
  부품6 = LSM303C (6 DOF)
  부품1 = Arduino Pro Mini (5V)
  S1 = Toggle Switch [package=THT]
  H1 = polarizedheader 4pin 0.156in [package=THT]
  LED3 = LED - 5mm [color="Red (633nm)" package="5 mm [THT]"]
  R1 = Resistor [tolerance=±5% resistance=220 package=THT]
  LED4 = RGB LED (com. cathode, rgb) [package="5 mm [THT]"]

nets:
  N1: 부품2.State, R1.Pin_1
  N2: 부품2.TXD, 부품1.D2
  N3: 부품2.RXD, 부품1.D3
  VCC: 부품2.VCC, 부품6.VDD_IO, 부품1.VCC, S1.COM, H1.pin2
  GND: 부품2.GND, X1.GND, 부품6.GND, 부품1.GND, S1.L1, H1.pin1, LED3.anode, LED4.common_cathode
  N4: X1.D+, U1.+
  N5: X1.D-, U1.-
  N6: X1.VBUS, S1.L2
  N7: 부품6.SDA/SDI/SDO, 부품1.A4
  N8: 부품6.SCL/SCLK, 부품1.A5
  N9: 부품1.TXO, H1.pin4
  N10: 부품1.RXI, H1.pin3
  N11: 부품1.MOSI, LED4.blue_anode
  N12: 부품1.D10, LED4.green_anode
  N13: 부품1.D9, LED4.red_anode
  N14: LED3.cathode, R1.Pin_0
